# Fritzing sketch Schematic_Amaze (saved by Fritzing 0.8.7b)
breadboards: 1

parts:
  Part1 = Arduino Uno (Rev3)
  Raspberry_Pi_1 = Raspberry Pi 4 [part_number=RPI-4-b]
  RFID1 = RFID Reader  # not connected
  Part2 = RFID USB Reader  # not connected
  SparkFun_OpenScale1 = openScale_v04 [part_number=SEN-13261]  # not connected
  R1 = PHOTOCELL [package=photocell-kit]
  LED1 = LED - 5mm [color="Red (633nm)" package="5 mm [THT]"]
  J1 = Basic Servo

nets:
  N1: Part1.A0, R1.P$1
  N2: Part1.D2, J1.pulse
  N3: Part1.D3_PWM, Raspberry_Pi_1.GPIO27
  N4: Part1.D4, Raspberry_Pi_1.GPIO17
  5V: Part1.5V, R1.P$2, LED1.anode, J1.vcc
  GND: Part1.GND, LED1.cathode, J1.gnd

custom parts:
  Raspberry Pi 4: The RPi4, a faster version of the awesome Raspberry Pi 2 B ARM Board with 40 pin gpio. Ready for special Raspberry Pi B+ and RPi2 Hat (Hardware attached (on) top)
  openScale_v04: OpenScale is an open source hardware load cell reader and calibration device. It has the ability to read multiple types of load cells and offers a simple to use serial menu to configure calibration value, sample rate, time stamp, and units of precision.
